// Logisim project imm-gen.circ as structural Verilog: 1 circuit, main circuit imm_gen
module imm_gen (
  input  [31:0] inst,
  input  [2:0] ImmSel,
  output [31:0] imm
);


  assign imm = {32{1'b0}};
  // also tied to GND on the sheet: {inst[7], inst[8], inst[9], inst[10], inst[11], inst[12], inst[13], inst[14], inst[15], inst[16], inst[17], inst[18], inst[19], inst[20], inst[21], inst[22], inst[23], inst[24], inst[25], inst[26], inst[27], inst[28], inst[29], inst[30], inst[31]}

  // Other names for the same wires on the sheet: B7 = inst[7]; B8_11[3:0] = inst[11:8]; B12_14[2:0] = inst[14:12];
  //   B15_19[4:0] = inst[19:15]; B20_24[4:0] = inst[24:20]; B25_30[5:0] = inst[30:25]; B31 = inst[31]

  // Notes on the sheet:
  //   INPUTS to your circuit
  //   DON'T CHANGE THE LOCATIONS OF THE INPUTS AND OUTPUTS!
  //   OUTPUT from your circuit
endmodule
